# Fritzing sketch 2 (saved by Fritzing 0.9.3b)
breadboards: 1

parts:
  Part7 = Adafruit HUZZAH32 ESP32 Feather [part_number="Adafruit #3405"]
  RHT2 = Humidity and Temperature Sensor RHT03
  R2 = Resistor [tolerance=±5% resistance=220 package=THT]

nets:
  N1: Part7.A5_IO4, RHT2.Data-signal, R2.Pin_0
  N2: Part7.GND, RHT2.GND_2
  3.3V: Part7.3.3V, RHT2.Vcc, R2.Pin_1
